# Fritzing sketch ConnectionESP_Arduino (saved by Fritzing 0.9.3b)
breadboards: 1

parts:
  Part1 = Arduino Uno (Rev3)
  U1 = ESP8266 WiFi Module [part_number=ESP8266]
  R2 = Resistor [tolerance=±5% resistance=1k package="0402 [SMD]"]  # not connected
  R3 = Resistor [tolerance=±5% resistance=2.2k package="0402 [SMD]"]

nets:
  N1: Part1.D6_PWM, U1.TXD
  3V3: Part1.3V3, U1.VCC, U1.CH_PD
  GND: Part1.GND, U1.GND, R3.Pin_0
  N2: U1.RXD, R3.Pin_1

custom parts:
  ESP8266 WiFi Module: Generic WiFi Module based on the ESP8266 with onboard PCB antenna and UART communications
